# Fritzing sketch robot (saved by Fritzing 0.9.3b)
breadboards: 1

parts:
  Part1 = Arduino Uno (Rev3)
  LED1 = LED - 5mm [color="Red (633nm)" package="5 mm [THT]"]
  hc-sr1 = hc-sr04
  R1 = Resistor [tolerance=±5% resistance=220 package="1206 [SMD]"]
  LED2 = LED - 5mm [color="Green (560nm)" package="5 mm [THT]"]
  R2 = Resistor [tolerance=±5% resistance=220 package="1206 [SMD]"]
  J1 = Piezo Speaker

nets:
  N1: Part1.D8, hc-sr1.Trig
  N2: Part1.D12/MISO, R1.Pin_1
  N3: Part1.D13/SCK, R2.Pin_1
  N4: Part1.D6_PWM, J1.pin2
  N5: Part1.D7, hc-sr1.Echo
  5V: Part1.5V, hc-sr1.VCC
  GND: Part1.GND, LED1.cathode, hc-sr1.GND, J1.pin1
  N6: LED1.anode, R1.Pin_0
  N7: LED2.anode, R2.Pin_0
